# Fritzing sketch fritzing_impose_output_voltage (saved by Fritzing 0.9.3b)
breadboards: 1

parts:
  U1 = 555 Timer [package="DIP8 [THT]"]

nets:
  N1: U1.Ground, U1.Threshold
  N2: U1.Control_Voltage, U1.Discharge

notes:
  MCP4911
  OUT
  Vdd
  Vss
  10
  13
  11
